# Fritzing sketch FTDI_SPIT_W_RPi_RESET_IN (saved by Fritzing 0.8.7b)
circuit board: 5.086cm x 3.84355cm
breadboards: 3

parts:
  S1 = Toggle Switch [package=THT]
  S2 = Toggle Switch [package=THT]
  JP4 = FTDI_BASIC [package=ftdi_basic]
  J1 = female pin header, 2 pins [form="♀ (female)"]
  R1 = Resistor [package="2010 [SMD]"]
  LED1 = LEDs [package=led10mm]
  JP3 = FTDI_BASIC [package=ftdi_basic]

nets:
  N1: S1.L1, JP4.6
  N2: S1.COM, JP3.1
  N3: S1.L2, J1.pin1
  N4: S2.L1, JP4.1
  N5: S2.COM, JP3.6
  N6: S2.L2, LED1.A
  N7: JP4.5, JP3.2
  N8: JP4.2, JP3.5
  N9: JP4.3, JP3.4
  N10: JP4.4, JP3.3
  N11: J1.pin2, R1.Pin_0
  N12: R1.Pin_1, LED1.C
